// Logisim project control-logic.circ as structural Verilog: 1 circuit, main circuit control_logic
module control_logic (
  input  [31:0] Instruction,
  input  BrEq,
  input  BrLt,
  output PCSel,
  output RegWEn,
  output [2:0] ImmSel,
  output BrUn,
  output ASel,
  output BSel,
  output [3:0] ALUSel,
  output MemRW,
  output [1:0] WBSel
);

  wire add, addi, and_22_out, and_23_out, and_24_out, and_25_out, and_26_out, and_27_out, and_28_out, andi,
       auipc, B_Type, beq, bge, bgeu, blt, bltu, bne, Branch, BType, comparator_1_eq, comparator_2_eq,
       comparator_3_eq, comparator_4_eq, comparator_5_eq, comparator_6_eq, comparator_7_eq, comparator_8_eq,
       comparator_9_eq, comparator_10_eq, comparator_11_eq, comparator_12_eq, comparator_15_eq,
       comparator_16_eq, comparator_17_eq, comparator_19_eq, comparator_20_eq, comparator_21_eq,
       comparator_22_eq, comparator_23_eq, comparator_24_eq, comparator_25_eq, comparator_26_eq,
       comparator_27_eq, comparator_28_eq, comparator_29_eq, comparator_30_eq, comparator_33_eq,
       comparator_34_eq, comparator_35_eq, comparator_36_eq, comparator_37_eq, comparator_38_eq,
       comparator_39_eq, comparator_40_eq, comparator_46_eq, comparator_47_eq, comparator_48_eq, exclusiveOR,
       I_Type, I_Type_Load, jal, jalr, lb, lh, lui, lw, mul, mulh, mulhu, not_1_out, not_2_out, not_3_out,
       ori, R_Type, R_Type_AND, R_Type_OR, S_Type, sb, sh, shiftLeft, shiftRightA, shiftRightL, slli, slt,
       slti, srai, srli, sub, sw, xori;
  wire [5:0] ROMinput;
  wire [15:14] rom_1_data;

  Comparator #(.width(10)) comparator_1 (
    .a({Instruction[31:25], Instruction[14:12]}), .b({10{1'b0}}), .eq(comparator_1_eq));  // open: gt, lt
  Comparator #(.width(10)) comparator_2 (
    .a({Instruction[31:25], Instruction[14:12]}), .b(10'h8), .eq(comparator_2_eq));  // open: gt, lt
  Comparator #(.width(10)) comparator_3 (
    .a({Instruction[31:25], Instruction[14:12]}), .b(10'h100), .eq(comparator_3_eq));  // open: gt, lt
  Comparator #(.width(10)) comparator_4 (
    .a({Instruction[31:25], Instruction[14:12]}), .b(10'h1), .eq(comparator_4_eq));  // open: gt, lt
  Comparator #(.width(10)) comparator_5 (
    .a({Instruction[31:25], Instruction[14:12]}), .b(10'h9), .eq(comparator_5_eq));  // open: gt, lt
  Comparator #(.width(10)) comparator_6 (
    .a({Instruction[31:25], Instruction[14:12]}), .b(10'hb), .eq(comparator_6_eq));  // open: gt, lt
  Comparator #(.width(10)) comparator_7 (
    .a({Instruction[31:25], Instruction[14:12]}), .b(10'h2), .eq(comparator_7_eq));  // open: gt, lt
  Comparator #(.width(10)) comparator_8 (
    .a({Instruction[31:25], Instruction[14:12]}), .b(10'h4), .eq(comparator_8_eq));  // open: gt, lt
  Comparator #(.width(10)) comparator_9 (
    .a({Instruction[31:25], Instruction[14:12]}), .b(10'h5), .eq(comparator_9_eq));  // open: gt, lt
  Comparator #(.width(10)) comparator_10 (
    .a({Instruction[31:25], Instruction[14:12]}), .b(10'h105), .eq(comparator_10_eq));  // open: gt, lt
  Comparator #(.width(10)) comparator_11 (
    .a({Instruction[31:25], Instruction[14:12]}), .b(10'h6), .eq(comparator_11_eq));  // open: gt, lt
  Comparator #(.width(10)) comparator_12 (
    .a({Instruction[31:25], Instruction[14:12]}), .b(10'h7), .eq(comparator_12_eq));  // open: gt, lt
  ROM #(.addrWidth(6), .dataWidth(16)) rom_1 (
    .addr(ROMinput), .data({rom_1_data, WBSel, MemRW, ALUSel, BSel, ASel, BrUn, ImmSel, RegWEn}));
  Comparator #(.width(7)) comparator_13 (.a(Instruction[6:0]), .b(7'b0110011), .eq(R_Type));  // open: gt, lt
  and and_1 (add, R_Type, comparator_1_eq);
  and and_2 (mul, R_Type, comparator_2_eq);
  and and_3 (sub, R_Type, comparator_3_eq);
  and and_4 (shiftLeft, R_Type, comparator_4_eq);
  and and_5 (mulh, R_Type, comparator_5_eq);
  and and_6 (mulhu, R_Type, comparator_6_eq);
  and and_7 (slt, R_Type, comparator_7_eq);
  and and_8 (exclusiveOR, R_Type, comparator_8_eq);
  and and_9 (shiftRightL, R_Type, comparator_9_eq);
  and and_10 (shiftRightA, R_Type, comparator_10_eq);
  and and_11 (R_Type_OR, R_Type, comparator_11_eq);
  and and_12 (R_Type_AND, R_Type, comparator_12_eq);
  Comparator #(.width(7)) comparator_14 (.a(Instruction[6:0]), .b(7'b0000011), .eq(I_Type_Load));  // open: gt, lt
  Comparator #(.width(3)) comparator_15 (.a(Instruction[14:12]), .b(3'b000), .eq(comparator_15_eq));  // open: gt, lt
  Comparator #(.width(3)) comparator_16 (.a(Instruction[14:12]), .b(3'b001), .eq(comparator_16_eq));  // open: gt, lt
  Comparator #(.width(3)) comparator_17 (.a(Instruction[14:12]), .b(3'b010), .eq(comparator_17_eq));  // open: gt, lt
  Comparator #(.width(7)) comparator_18 (.a(Instruction[6:0]), .b(7'b1100011), .eq(B_Type));  // open: gt, lt
  Comparator #(.width(3)) comparator_19 (.a(Instruction[14:12]), .b(3'b000), .eq(comparator_19_eq));  // open: gt, lt
  Comparator #(.width(3)) comparator_20 (.a(Instruction[14:12]), .b(3'b001), .eq(comparator_20_eq));  // open: gt, lt
  Comparator #(.width(3)) comparator_21 (.a(Instruction[14:12]), .b(3'b100), .eq(comparator_21_eq));  // open: gt, lt
  Comparator #(.width(3)) comparator_22 (.a(Instruction[14:12]), .b(3'b101), .eq(comparator_22_eq));  // open: gt, lt
  Comparator #(.width(3)) comparator_23 (.a(Instruction[14:12]), .b(3'b110), .eq(comparator_23_eq));  // open: gt, lt
  Comparator #(.width(3)) comparator_24 (.a(Instruction[14:12]), .b(3'b111), .eq(comparator_24_eq));  // open: gt, lt
  Comparator #(.width(3)) comparator_25 (.a(Instruction[14:12]), .b(3'b000), .eq(comparator_25_eq));  // open: gt, lt
  Comparator #(.width(3)) comparator_26 (.a(Instruction[14:12]), .b(3'b001), .eq(comparator_26_eq));  // open: gt, lt
  Comparator #(.width(3)) comparator_27 (.a(Instruction[14:12]), .b(3'b100), .eq(comparator_27_eq));  // open: gt, lt
  Comparator #(.width(3)) comparator_28 (.a(Instruction[14:12]), .b(3'b110), .eq(comparator_28_eq));  // open: gt, lt
  Comparator #(.width(3)) comparator_29 (.a(Instruction[14:12]), .b(3'b101), .eq(comparator_29_eq));  // open: gt, lt
  Comparator #(.width(3)) comparator_30 (.a(Instruction[14:12]), .b(3'b111), .eq(comparator_30_eq));  // open: gt, lt
  and and_13 (lb, I_Type_Load, comparator_15_eq);
  and and_14 (lh, I_Type_Load, comparator_16_eq);
  and and_15 (lw, I_Type_Load, comparator_17_eq);
  and and_16 (beq, B_Type, comparator_19_eq);
  and and_17 (bne, B_Type, comparator_20_eq);
  and and_18 (blt, B_Type, comparator_21_eq);
  and and_19 (bge, B_Type, comparator_22_eq);
  and and_20 (bltu, B_Type, comparator_23_eq);
  and and_21 (bgeu, B_Type, comparator_24_eq);
  Comparator #(.width(7)) comparator_31 (.a(Instruction[6:0]), .b(7'b1100011), .eq(BType));  // open: gt, lt
  not not_1 (not_1_out, BrEq);
  not not_2 (not_2_out, BrLt);
  not not_3 (not_3_out, BrLt);
  and and_22 (and_22_out, comparator_25_eq, BrEq);
  and and_23 (and_23_out, comparator_26_eq, not_1_out);
  and and_24 (and_24_out, comparator_27_eq, BrLt);
  and and_25 (and_25_out, comparator_28_eq, BrLt);
  and and_26 (and_26_out, comparator_29_eq, not_2_out);
  and and_27 (and_27_out, comparator_30_eq, not_3_out);
  and and_28 (and_28_out, BType, Branch);
  or or_1 (PCSel, jal, jalr, and_28_out);
  Comparator #(.width(7)) comparator_32 (.a(Instruction[6:0]), .b(7'b0010011), .eq(I_Type));  // open: gt, lt
  Comparator #(.width(3)) comparator_33 (.a(Instruction[14:12]), .b(3'b000), .eq(comparator_33_eq));  // open: gt, lt
  Comparator #(.width(3)) comparator_34 (.a(Instruction[14:12]), .b(3'b001), .eq(comparator_34_eq));  // open: gt, lt
  Comparator #(.width(3)) comparator_35 (.a(Instruction[14:12]), .b(3'b010), .eq(comparator_35_eq));  // open: gt, lt
  Comparator #(.width(3)) comparator_36 (.a(Instruction[14:12]), .b(3'b100), .eq(comparator_36_eq));  // open: gt, lt
  Comparator #(.width(10)) comparator_37 (
    .a({Instruction[31:25], Instruction[14:12]}), .b(10'h5), .eq(comparator_37_eq));  // open: gt, lt
  Comparator #(.width(10)) comparator_38 (
    .a({Instruction[31:25], Instruction[14:12]}), .b(10'h105), .eq(comparator_38_eq));  // open: gt, lt
  Comparator #(.width(3)) comparator_39 (.a(Instruction[14:12]), .b(3'b110), .eq(comparator_39_eq));  // open: gt, lt
  Comparator #(.width(3)) comparator_40 (.a(Instruction[14:12]), .b(3'b111), .eq(comparator_40_eq));  // open: gt, lt
  or or_2 (Branch, and_22_out, and_23_out, and_24_out, and_25_out, and_26_out, and_27_out);
  and and_29 (addi, I_Type, comparator_33_eq);
  and and_30 (slli, I_Type, comparator_34_eq);
  and and_31 (slti, I_Type, comparator_35_eq);
  and and_32 (xori, I_Type, comparator_36_eq);
  and and_33 (srli, I_Type, comparator_37_eq);
  and and_34 (srai, I_Type, comparator_38_eq);
  and and_35 (ori, I_Type, comparator_39_eq);
  and and_36 (andi, I_Type, comparator_40_eq);
  Comparator #(.width(7)) comparator_41 (.a(Instruction[6:0]), .b(7'b0010111), .eq(auipc));  // open: gt, lt
  Comparator #(.width(7)) comparator_42 (.a(Instruction[6:0]), .b(7'b0110111), .eq(lui));  // open: gt, lt
  Comparator #(.width(7)) comparator_43 (.a(Instruction[6:0]), .b(7'b1101111), .eq(jal));  // open: gt, lt
  Comparator #(.width(7)) comparator_44 (.a(Instruction[6:0]), .b(7'b1100111), .eq(jalr));  // open: gt, lt
  Comparator #(.width(7)) comparator_45 (.a(Instruction[6:0]), .b(7'b0100011), .eq(S_Type));  // open: gt, lt
  Comparator #(.width(3)) comparator_46 (.a(Instruction[14:12]), .b(3'b000), .eq(comparator_46_eq));  // open: gt, lt
  Comparator #(.width(3)) comparator_47 (.a(Instruction[14:12]), .b(3'b001), .eq(comparator_47_eq));  // open: gt, lt
  Comparator #(.width(3)) comparator_48 (.a(Instruction[14:12]), .b(3'b010), .eq(comparator_48_eq));  // open: gt, lt
  and and_37 (sb, S_Type, comparator_46_eq);
  and and_38 (sh, S_Type, comparator_47_eq);
  and and_39 (sw, S_Type, comparator_48_eq);
  Priority_Encoder #(.select_enc(6)) priority_encoder_1 (
    .in0(add), .in1(mul), .in2(sub), .in3(shiftLeft), .in4(mulh), .in5(mulhu), .in6(slt), .in7(exclusiveOR),
    .in8(shiftRightL), .in9(shiftRightA), .in10(R_Type_OR), .in11(R_Type_AND), .in12(lb), .in13(lh),
    .in14(lw), .in15(addi), .in16(slli), .in17(slti), .in18(xori), .in19(srli), .in20(srai), .in21(ori),
    .in22(andi), .in23(sb), .in24(sh), .in25(sw), .in26(beq), .in27(bne), .in28(blt), .in29(bge),
    .in30(bltu), .in31(bgeu), .in32(auipc), .in33(lui), .in34(jal), .in35(jalr), .out(ROMinput));  // open: in36, in37, in38, in39, in40, in41, in42, in43, in44, in45, in46, in47, in48, in49, in50, in51, in52, in53, in54, in55, in56, in57, in58, in59, in60, in61, in62, in63, gs, en_out, en_in
  // Probe on ROMinput

  // Notes on the sheet:
  //   INPUTS to your circuit
  //   Connect ROM Input here ->
  //   contents of rom_1 (hex, n*v repeats v):
  //   100f 140f 160f 108f 148f 158f 110f 120f 128f 168f 130f 138f 41 41 41 1041 10c1 1141 1241 12c1 16c1
  //   1341 13c1 842 842 842 4*64 74 74 1067 17c7 2069 2041
  //   ROM FOR CONTROL LOGIC
  //   DON'T CHANGE THE LOCATIONS OF THE INPUTS AND OUTPUTS!
  //   This is only if you choose to do the ROM option
  //   CONNECT
  //   WIRE
  //   TO
  //   USE
  //   ROM
  //   OUTPUT from your circuit
  //   Reminder: If using ROM, use combinational logic for PCSel
endmodule
