// Logisim project partial-store.circ as structural Verilog: 1 circuit, main circuit partial_store
module partial_store (
  input  [31:0] Instruction,
  input  [31:0] MemAddress,
  input  [31:0] DataFromReg,
  input  MemRW,
  output [3:0] MemWriteMask,
  output [31:0] DataToMem
);

  wire [3:0] multiplexer_6_out, sbMask, shMask;
  wire [31:0] multiplexer_3_out, sb, sh;

  Demultiplexer #(.select(2), .width(8)) demultiplexer_1 (
    .out0(sb[7:0]), .out1(sb[15:8]), .out2(sb[23:16]), .out3(sb[31:24]), .in(DataFromReg[7:0]),
    .sel(MemAddress[1:0]));
  Demultiplexer #(.select(2), .width(16)) demultiplexer_2 (
    .out0(sh[15:0]), .out2(sh[31:16]), .in(DataFromReg[15:0]), .sel(MemAddress[1:0]));  // open: out1, out3
  Multiplexer #(.select(2), .width(4)) multiplexer_1 (
    .in0(4'b0001), .in1(4'b0010), .in2(4'b0100), .in3(4'b1000), .out(sbMask), .sel(MemAddress[1:0]));
  Multiplexer #(.select(2), .width(4)) multiplexer_2 (
    .in0(4'b0011), .in2(4'b1100), .out(shMask), .sel(MemAddress[1:0]));  // open: in1, in3
  Multiplexer #(.select(2), .width(32)) multiplexer_3 (
    .in0(sb), .in1(sh), .in2(DataFromReg), .out(multiplexer_3_out), .sel(Instruction[13:12]));  // open: in3
  Multiplexer #(.width(32)) multiplexer_4 (.in0({32{1'b0}}), .in1(multiplexer_3_out), .out(DataToMem), .sel(MemRW));
  Multiplexer #(.width(4)) multiplexer_5 (.in0(4'b0000), .in1(multiplexer_6_out), .out(MemWriteMask), .sel(MemRW));
  Multiplexer #(.select(2), .width(4)) multiplexer_6 (
    .in0(sbMask), .in1(shMask), .in2(4'b1111), .out(multiplexer_6_out), .sel(Instruction[13:12]));  // open: in3

  // Other names for the same wires on the sheet: offset[1:0] = MemAddress[1:0]

  // Notes on the sheet:
  //   INPUTS to your circuit
  //   DON'T CHANGE THE LOCATIONS OF THE INPUTS AND OUTPUTS!
  //   OUTPUT from your circuit
endmodule
